// Logisim project circuito.circ as structural Verilog: 1 circuit, main circuit main
module main (
  input  in_1,
  input  in_2,
  input  in_3,
  input  in_4,
  input  in_5,
  input  in_6,
  input  in_7,
  input  in_8,
  input  in_9,
  input  in_10,
  input  in_11,
  input  in_12,
  input  in_13,
  input  in_14,
  input  M1,
  input  M2,
  input  M3,
  input  Tobi,
  output out_19,
  output out_20,
  output out_21,
  output out_22,
  output out_23,
  output out_24
);

  wire and_1_out, and_2_out, and_3_out, and_4_out, and_5_out, and_6_out, and_7_out, and_8_out, not_1_out,
       not_2_out, not_3_out, not_4_out, not_5_out, not_6_out, not_7_out, not_8_out, or_1_out, or_2_out;

  not not_1 (not_1_out, in_1);
  not not_2 (not_2_out, in_2);
  not not_3 (not_3_out, in_3);
  not not_4 (not_4_out, in_6);
  not not_5 (not_5_out, in_9);
  not not_6 (not_6_out, in_10);
  not not_7 (not_7_out, in_11);
  not not_8 (not_8_out, in_14);
  and and_1 (and_1_out, in_7, in_8);
  and and_2 (and_2_out, not_5_out, not_6_out);
  or or_1 (or_1_out, not_7_out, in_12);
  or or_2 (or_2_out, in_13, not_8_out);
  and and_3 (and_3_out, M1, Tobi);
  and and_4 (and_4_out, M2, Tobi);
  and and_5 (and_5_out, M3, Tobi);
  and and_6 (and_6_out, M1, M2, M3);
  and and_7 (and_7_out, not_1_out, not_2_out);
  or or_3 (out_20, not_3_out, in_4);
  not not_9 (out_21, and_8_out);
  and and_8 (and_8_out, in_5, not_4_out);
  not not_10 (out_19, and_7_out);
  or or_4 (out_22, and_1_out, and_2_out);
  and and_9 (out_23, or_1_out, or_2_out);
  or or_5 (out_24, and_3_out, and_4_out, and_5_out, and_6_out);

  // Notes on the sheet:
  //   CIRCUITO 1: OR
  //   CIRUITO 2 : IMPLICACIÓN
  //   CIRCUITO 4 : MECANISMO DE VOTACIÓN
  //   CIRCUITO 3: DOBLE IMPLICACIÓN
  //   Circuito que modela una implicación
  //   Circuito que es equivalente al anterior
  //   Circuito Or sin usar la puerta OR
  //   Circuito que modela una doble implicación
  //   Circuito equivalente al anterior
endmodule
