// Logisim project circuito.circ as structural Verilog: 1 circuit, main circuit main
module main (
  input  W,
  input  X,
  input  Y,
  input  Z,
  input  M1,
  input  M2,
  input  M3,
  output out_8,
  output out_9
);

  wire and_1_out, and_2_out, and_3_out, and_4_out, and_5_out, not_1_out, not_2_out;

  not not_1 (not_1_out, X);
  not not_2 (not_2_out, Y);
  and and_1 (and_1_out, M1, M3);
  and and_2 (and_2_out, M2, M3);
  and and_3 (and_3_out, M1, M2);
  and and_4 (and_4_out, W, X);
  and and_5 (and_5_out, not_1_out, not_2_out, Z);
  or or_1 (out_9, and_1_out, and_2_out, and_3_out);
  or or_2 (out_8, and_4_out, and_5_out);

  // Notes on the sheet:
  //   REDUCCIÓN
  //   MOTÍN
endmodule
