// Logisim project circuito.circ as structural Verilog: 1 circuit, main circuit main
module main (
  input  X2,
  input  X1,
  input  X0,
  input  X1_2,
  input  X2_2,
  input  X3,
  output out_7,
  output out_8,
  output out_9,
  output out_10,
  output out_11,
  output out_12,
  output out_13,
  output out_14,
  output out_15
);

  wire and_9_out, and_10_out, and_11_out, and_12_out, not_1_out, not_2_out, not_3_out, not_4_out, not_5_out,
       not_6_out;

  not not_1 (not_1_out, X2);
  not not_2 (not_2_out, X1);
  not not_3 (not_3_out, X0);
  and and_1 (out_7, not_1_out, not_2_out, not_3_out);
  and and_2 (out_8, not_1_out, not_2_out, X0);
  and and_3 (out_9, not_1_out, X1, not_3_out);
  and and_4 (out_11, not_1_out, X1, X0);
  and and_5 (out_12, X2, not_2_out, not_3_out);
  and and_6 (out_13, X2, not_2_out, X0);
  and and_7 (out_14, X2, X1, not_3_out);
  and and_8 (out_15, X2, X1, X0);
  not not_4 (not_4_out, X1_2);
  not not_5 (not_5_out, X2_2);
  not not_6 (not_6_out, X3);
  and and_9 (and_9_out, not_4_out, X2_2, X3);
  and and_10 (and_10_out, X1_2, not_5_out, X3);
  and and_11 (and_11_out, X1_2, X2_2, not_6_out);
  and and_12 (and_12_out, X1_2, X2_2, X3);
  or or_1 (out_10, and_9_out, and_10_out, and_11_out, and_12_out);

  // Notes on the sheet:
  //   Decodificador de 3x8
  //   Decodificador Toby
  //   Fiesta Sorpresa
endmodule
