// Logisim project circuito.circ as structural Verilog: 1 circuit, main circuit main
module main (
  input  A,
  input  [7:0] A_2,
  input  B,
  input  C0,
  input  [7:0] B_2,
  output S,
  output [7:0] out_7,
  output Acarreo,
  output C
);

  wire and_1_out, and_2_out, xor_1_out;

  xor xor_1 (xor_1_out, A, B);
  and and_1 (and_1_out, A, B);
  xor xor_2 (S, xor_1_out, C0);
  and and_2 (and_2_out, xor_1_out, C0);
  or or_1 (C, and_2_out, and_1_out);
  Adder adder_1 (.a(A_2), .b(B_2), .out(out_7), .cout(Acarreo));  // open: cin

  // Notes on the sheet:
  //   CIRCUITO 1:Sumador completo
  //   CIRCUITO 2:Sumador de 8 bits
  //   Salida
endmodule
