// Logisim project circuito.circ as structural Verilog: 2 circuits, main circuit main
module main (
);

  wire and_1_out, and_2_out, and_3_out, and_4_out, and_5_out, bcd_1_a_2, bcd_1_b_2, bcd_1_c_2, bcd_1_d_2,
       bcd_1_e, bcd_1_f, bcd_1_g, bcd_2_a_2, bcd_2_b_2, bcd_2_c_2, bcd_2_d_2, bcd_2_e, bcd_2_f, bcd_2_g,
       bcd_3_a_2, bcd_3_b_2, bcd_3_c_2, bcd_3_d_2, bcd_3_e, bcd_3_f, bcd_3_g, bcd_4_a_2, bcd_4_b_2,
       bcd_4_c_2, bcd_4_d_2, bcd_4_e, bcd_4_f, bcd_4_g, clock_1_out, clock_2_out, clock_3_out, j_k_ff_1_q,
       j_k_ff_1_qn, j_k_ff_2_q, j_k_ff_2_qn, j_k_ff_3_q, j_k_ff_3_qn, j_k_ff_4_q, j_k_ff_4_qn, j_k_ff_5_q,
       j_k_ff_5_qn, j_k_ff_6_q, j_k_ff_6_qn, j_k_ff_7_q, j_k_ff_7_qn, j_k_ff_8_q, j_k_ff_8_qn, j_k_ff_9_q,
       j_k_ff_9_qn, j_k_ff_10_q, j_k_ff_10_qn, j_k_ff_11_q, j_k_ff_11_qn, j_k_ff_12_q, j_k_ff_12_qn,
       j_k_ff_13_q, j_k_ff_13_qn, j_k_ff_14_q, j_k_ff_14_qn, j_k_ff_15_q, j_k_ff_15_qn, j_k_ff_16_q,
       j_k_ff_17_q, j_k_ff_18_q, j_k_ff_19_q, j_k_ff_20_q, or_1_out;

  Clock clock_1 (.out(clock_1_out));
  Clock clock_2 (.out(clock_2_out));
  Clock clock_3 (.out(clock_3_out));
  or or_1 (or_1_out, and_2_out, and_1_out);
  J_K_Flip_Flop j_k_ff_1 (
    .J(1'b1), .clk(clock_1_out), .K(1'b1), .Q(j_k_ff_1_q), .Qn(j_k_ff_1_qn), .en(1'b1), .reset(and_3_out));  // open: preset
  J_K_Flip_Flop j_k_ff_2 (
    .J(1'b1), .clk(clock_2_out), .K(1'b1), .Q(j_k_ff_2_q), .Qn(j_k_ff_2_qn), .en(1'b1), .reset(and_4_out));  // open: preset
  J_K_Flip_Flop j_k_ff_3 (
    .J(1'b1), .clk(clock_3_out), .K(1'b1), .Q(j_k_ff_3_q), .Qn(j_k_ff_3_qn), .reset(and_5_out));  // open: preset, en
  and and_1 (and_1_out, j_k_ff_19_q, j_k_ff_9_q);
  J_K_Flip_Flop j_k_ff_4 (
    .J(1'b1), .clk(and_5_out), .K(1'b1), .Q(j_k_ff_4_q), .Qn(j_k_ff_4_qn), .reset(and_1_out));  // open: preset, en
  and and_2 (and_2_out, j_k_ff_20_q, j_k_ff_10_q);
  J_K_Flip_Flop j_k_ff_5 (
    .J(1'b1), .clk(or_1_out), .K(1'b1), .Q(j_k_ff_5_q), .Qn(j_k_ff_5_qn), .reset(and_2_out));  // open: preset, en
  and and_3 (and_3_out, j_k_ff_16_q, j_k_ff_6_q);
  and and_4 (and_4_out, j_k_ff_17_q, j_k_ff_7_q);
  and and_5 (and_5_out, j_k_ff_18_q, j_k_ff_8_q);
  J_K_Flip_Flop j_k_ff_6 (
    .J(1'b1), .clk(j_k_ff_1_qn), .K(1'b1), .Q(j_k_ff_6_q), .Qn(j_k_ff_6_qn), .en(1'b1), .reset(and_3_out));  // open: preset
  LED led_1 (.in(j_k_ff_11_q));
  LED led_2 (.in(j_k_ff_16_q));
  J_K_Flip_Flop j_k_ff_7 (
    .J(1'b1), .clk(j_k_ff_2_qn), .K(1'b1), .Q(j_k_ff_7_q), .Qn(j_k_ff_7_qn), .en(1'b1), .reset(and_4_out));  // open: preset
  J_K_Flip_Flop j_k_ff_8 (
    .J(1'b1), .clk(j_k_ff_3_qn), .K(1'b1), .Q(j_k_ff_8_q), .Qn(j_k_ff_8_qn), .en(1'b1), .reset(and_5_out));  // open: preset
  J_K_Flip_Flop j_k_ff_9 (
    .J(1'b1), .clk(j_k_ff_4_qn), .K(1'b1), .Q(j_k_ff_9_q), .Qn(j_k_ff_9_qn), .reset(and_1_out));  // open: preset, en
  J_K_Flip_Flop j_k_ff_10 (
    .J(1'b1), .clk(j_k_ff_5_qn), .K(1'b1), .Q(j_k_ff_10_q), .Qn(j_k_ff_10_qn), .reset(and_2_out));  // open: preset, en
  J_K_Flip_Flop j_k_ff_11 (
    .J(1'b1), .clk(j_k_ff_6_qn), .K(1'b1), .Q(j_k_ff_11_q), .Qn(j_k_ff_11_qn), .en(1'b1), .reset(and_3_out));  // open: preset
  LED led_3 (.in(j_k_ff_6_q));
  LED led_4 (.in(j_k_ff_1_q));
  J_K_Flip_Flop j_k_ff_12 (
    .J(1'b1), .clk(j_k_ff_7_qn), .K(1'b1), .Q(j_k_ff_12_q), .Qn(j_k_ff_12_qn), .en(1'b1), .reset(and_4_out));  // open: preset
  J_K_Flip_Flop j_k_ff_13 (
    .J(1'b1), .clk(j_k_ff_8_qn), .K(1'b1), .Q(j_k_ff_13_q), .Qn(j_k_ff_13_qn), .en(1'b1), .reset(and_5_out));  // open: preset
  J_K_Flip_Flop j_k_ff_14 (
    .J(1'b1), .clk(j_k_ff_9_qn), .K(1'b1), .Q(j_k_ff_14_q), .Qn(j_k_ff_14_qn), .reset(and_1_out));  // open: preset, en
  J_K_Flip_Flop j_k_ff_15 (
    .J(1'b1), .clk(j_k_ff_10_qn), .K(1'b1), .Q(j_k_ff_15_q), .Qn(j_k_ff_15_qn), .reset(and_2_out));  // open: preset, en
  J_K_Flip_Flop j_k_ff_16 (
    .J(1'b1), .clk(j_k_ff_11_qn), .K(1'b1), .Q(j_k_ff_16_q), .en(1'b1), .reset(and_3_out));  // open: Qn, preset
  J_K_Flip_Flop j_k_ff_17 (
    .J(1'b1), .clk(j_k_ff_12_qn), .K(1'b1), .Q(j_k_ff_17_q), .en(1'b1), .reset(and_4_out));  // open: Qn, preset
  J_K_Flip_Flop j_k_ff_18 (
    .J(1'b1), .clk(j_k_ff_13_qn), .K(1'b1), .Q(j_k_ff_18_q), .en(1'b1), .reset(and_5_out));  // open: Qn, preset
  J_K_Flip_Flop j_k_ff_19 (
    .J(1'b1), .clk(j_k_ff_14_qn), .K(1'b1), .Q(j_k_ff_19_q), .reset(and_1_out));  // open: Qn, preset, en
  J_K_Flip_Flop j_k_ff_20 (
    .J(1'b1), .clk(j_k_ff_15_qn), .K(1'b1), .Q(j_k_ff_20_q), .reset(and_2_out));  // open: Qn, preset, en
  bcd bcd_1 (
    .D(j_k_ff_17_q), .C(j_k_ff_12_q), .B(j_k_ff_7_q), .A(j_k_ff_2_q), .a_2(bcd_1_a_2), .b_2(bcd_1_b_2),
    .c_2(bcd_1_c_2), .d_2(bcd_1_d_2), .e(bcd_1_e), .f(bcd_1_f), .g(bcd_1_g));
  bcd bcd_2 (
    .D(j_k_ff_18_q), .C(j_k_ff_13_q), .B(j_k_ff_8_q), .A(j_k_ff_3_q), .a_2(bcd_2_a_2), .b_2(bcd_2_b_2),
    .c_2(bcd_2_c_2), .d_2(bcd_2_d_2), .e(bcd_2_e), .f(bcd_2_f), .g(bcd_2_g));
  bcd bcd_3 (
    .D(j_k_ff_19_q), .C(j_k_ff_14_q), .B(j_k_ff_9_q), .A(j_k_ff_4_q), .a_2(bcd_3_a_2), .b_2(bcd_3_b_2),
    .c_2(bcd_3_c_2), .d_2(bcd_3_d_2), .e(bcd_3_e), .f(bcd_3_f), .g(bcd_3_g));
  bcd bcd_4 (
    .D(j_k_ff_20_q), .C(j_k_ff_15_q), .B(j_k_ff_10_q), .A(j_k_ff_5_q), .a_2(bcd_4_a_2), .b_2(bcd_4_b_2),
    .c_2(bcd_4_c_2), .d_2(bcd_4_d_2), .e(bcd_4_e), .f(bcd_4_f), .g(bcd_4_g));
  _7_Segment_Display u_7_segment_display_1 (
    .g(bcd_1_g), .f(bcd_1_f), .a(bcd_1_a_2), .b(bcd_1_b_2), .e(bcd_1_e), .d(bcd_1_d_2), .c(bcd_1_c_2));  // open: dp
  _7_Segment_Display u_7_segment_display_2 (
    .g(bcd_2_g), .f(bcd_2_f), .a(bcd_2_a_2), .b(bcd_2_b_2), .e(bcd_2_e), .d(bcd_2_d_2), .c(bcd_2_c_2));  // open: dp
  _7_Segment_Display u_7_segment_display_3 (
    .g(bcd_3_g), .f(bcd_3_f), .a(bcd_3_a_2), .b(bcd_3_b_2), .e(bcd_3_e), .d(bcd_3_d_2), .c(bcd_3_c_2));  // open: dp
  _7_Segment_Display u_7_segment_display_4 (
    .g(bcd_4_g), .f(bcd_4_f), .a(bcd_4_a_2), .b(bcd_4_b_2), .e(bcd_4_e), .d(bcd_4_d_2), .c(bcd_4_c_2));  // open: dp

  // Notes on the sheet:
  //   CIRCUITO 1
  //   CIRCUITO 2
  //   CIRCUITO 3
endmodule

module bcd (
  input  D,
  input  C,
  input  B,
  input  A,
  output a_2,
  output b_2,
  output c_2,
  output d_2,
  output e,
  output f,
  output g
);

  wire and_1_out, and_2_out, and_3_out, and_4_out, and_5_out, and_6_out, and_7_out, and_8_out, and_9_out,
       and_10_out, and_11_out, and_12_out, and_13_out, and_14_out, and_15_out, and_16_out, not_1_out,
       not_2_out, not_3_out, not_4_out, not_5_out, not_6_out, not_7_out, not_8_out, not_9_out, not_10_out,
       not_11_out, not_12_out, not_13_out, not_14_out, not_15_out, not_16_out, not_17_out, not_18_out,
       not_19_out, not_20_out, not_21_out;

  not not_1 (not_1_out, C);
  and and_1 (and_1_out, not_1_out, not_2_out);
  not not_2 (not_2_out, A);
  and and_2 (and_2_out, C, A);
  not not_3 (not_3_out, C);
  not not_4 (not_4_out, B);
  and and_3 (and_3_out, not_4_out, not_5_out);
  not not_5 (not_5_out, A);
  and and_4 (and_4_out, B, A);
  not not_6 (not_6_out, B);
  or or_1 (c_2, not_6_out, A, C);
  not not_7 (not_7_out, C);
  and and_5 (and_5_out, not_7_out, not_8_out);
  not not_8 (not_8_out, A);
  not not_9 (not_9_out, C);
  and and_6 (and_6_out, not_9_out, B);
  and and_7 (and_7_out, B, not_10_out);
  not not_10 (not_10_out, A);
  and and_8 (and_8_out, C, not_11_out, A);
  not not_11 (not_11_out, B);
  not not_12 (not_12_out, C);
  and and_9 (and_9_out, not_12_out, not_13_out);
  not not_13 (not_13_out, A);
  and and_10 (and_10_out, B, not_14_out);
  not not_14 (not_14_out, A);
  not not_15 (not_15_out, B);
  and and_11 (and_11_out, not_15_out, not_16_out);
  not not_16 (not_16_out, A);
  and and_12 (and_12_out, C, not_17_out);
  not not_17 (not_17_out, B);
  and and_13 (and_13_out, C, not_18_out);
  not not_18 (not_18_out, A);
  not not_19 (not_19_out, C);
  and and_14 (and_14_out, not_19_out, B);
  and and_15 (and_15_out, C, not_20_out);
  not not_20 (not_20_out, B);
  and and_16 (and_16_out, C, not_21_out);
  not not_21 (not_21_out, A);
  or or_2 (a_2, and_1_out, B, and_2_out, D);
  or or_3 (b_2, not_3_out, and_3_out, and_4_out);
  or or_4 (d_2, and_5_out, and_6_out, and_7_out, and_8_out, D);
  or or_5 (e, and_9_out, and_10_out);
  or or_6 (f, and_11_out, and_12_out, and_13_out, D);
  or or_7 (g, and_14_out, and_15_out, and_16_out, D);
endmodule
