// Logisim project circuito.circ as structural Verilog: 2 circuits, main circuit main
module main (
  input  [7:0] A,
  input  [7:0] B,
  input  [1:0] Op,
  output [7:0] Salida
);

  wire alu_1_bit_1_carryout, alu_1_bit_2_carryout, alu_1_bit_3_carryout, alu_1_bit_4_carryout,
       alu_1_bit_5_carryout, alu_1_bit_6_carryout, alu_1_bit_7_carryout, decoder_1_out3;

  ALU___1_bit alu_1_bit_1 (
    .A(A[0]), .B(B[0]), .CarryIn(decoder_1_out3), .CarryOut(alu_1_bit_1_carryout), .Op(Op), .out_5(Salida[0]));
  ALU___1_bit alu_1_bit_2 (
    .A(A[1]), .B(B[1]), .CarryIn(alu_1_bit_1_carryout), .CarryOut(alu_1_bit_2_carryout), .Op(Op),
    .out_5(Salida[1]));
  ALU___1_bit alu_1_bit_3 (
    .A(A[2]), .B(B[2]), .CarryIn(alu_1_bit_2_carryout), .CarryOut(alu_1_bit_3_carryout), .Op(Op),
    .out_5(Salida[2]));
  ALU___1_bit alu_1_bit_4 (
    .A(A[3]), .B(B[3]), .CarryIn(alu_1_bit_3_carryout), .CarryOut(alu_1_bit_4_carryout), .Op(Op),
    .out_5(Salida[3]));
  ALU___1_bit alu_1_bit_5 (
    .A(A[4]), .B(B[4]), .CarryIn(alu_1_bit_4_carryout), .CarryOut(alu_1_bit_5_carryout), .Op(Op),
    .out_5(Salida[4]));
  ALU___1_bit alu_1_bit_6 (
    .A(A[5]), .B(B[5]), .CarryIn(alu_1_bit_5_carryout), .CarryOut(alu_1_bit_6_carryout), .Op(Op),
    .out_5(Salida[5]));
  ALU___1_bit alu_1_bit_7 (
    .A(A[6]), .B(B[6]), .CarryIn(alu_1_bit_6_carryout), .CarryOut(alu_1_bit_7_carryout), .Op(Op),
    .out_5(Salida[6]));
  ALU___1_bit alu_1_bit_8 (
    .A(A[7]), .B(B[7]), .CarryIn(alu_1_bit_7_carryout), .Op(Op), .out_5(Salida[7]));  // open: CarryOut
  Decoder #(.select(2), .enable("false")) decoder_1 (.out3(decoder_1_out3), .sel(Op));  // open: out0, out1, out2

  // Notes on the sheet:
  //   AND=00
  //   OR=01
  //   SUMA=10
  //   RESTA =11
  //   ALU de 8 bits
endmodule

module ALU___1_bit (
  input  A,
  input  B,
  input  [1:0] Op,
  input  CarryIn,
  output out_5,
  output CarryOut
);

  wire adder_1_out, and_1_out, decoder_1_out3, multiplexer_1_out, not_1_out, or_1_out;

  Multiplexer #(.enable("false")) multiplexer_1 (
    .in0(B), .in1(not_1_out), .out(multiplexer_1_out), .sel(decoder_1_out3));
  not not_1 (not_1_out, B);
  and and_1 (and_1_out, A, B);
  or or_1 (or_1_out, A, B);
  Adder #(.width(1)) adder_1 (.a(A), .b(multiplexer_1_out), .out(adder_1_out), .cin(CarryIn), .cout(CarryOut));
  Multiplexer #(.select(2), .enable("false")) multiplexer_2 (
    .in0(and_1_out), .in1(or_1_out), .in2(adder_1_out), .in3(adder_1_out), .out(out_5), .sel(Op));
  Decoder #(.select(2), .enable("false")) decoder_1 (.out3(decoder_1_out3), .sel(Op));  // open: out0, out1, out2

  // Notes on the sheet:
  //   OPERACIONES
  //   AND=00
  //   OR=01
  //   SUMA=10
  //   RESTA =11
endmodule
